# Fritzing sketch o3box (saved by Fritzing 0.9.3b)
breadboards: 1

parts:
  Componente1 = Arduino Uno (Rev3) - ICSP
  U1 = GAS_SENSOR [package=mq-3]
  U2 = GAS_SENSOR [package=mq-3]
  Componente3 = LCD1602-I2C
  SW1 = ENCODER_RGB_CA [package=encoder_led_3]
  Part1 = KY-016 RGB Full Color LED Module [package="Breakout board"]
  J1 = Piezo Speaker

nets:
  N1: Componente1.A0, U2.H1
  N2: Componente1.A1, U1.H2
  N3: Componente1.A4/SDA, Componente3.SDA
  N4: Componente1.A5/SCL, Componente3.SCL
  N5: Componente1.ICSP_MOSI, Componente1.D11_PWM/MOSI, Part1.B
  N6: Componente1.D9_PWM, Part1.R
  N7: Componente1.D10_PWM/SS, Part1.G
  GND: Componente1.GND, U1.B1, U2.B1, Componente3.GND, SW1.-B, Part1.-, J1.pin1
  N8: Componente1.D4, J1.pin2
  N9: Componente1.D5_PWM, SW1.A
  N10: Componente1.D6_PWM, SW1.C
  N11: Componente1.D7, SW1.B
  5V: Componente1.5V, U1.A1, U2.A1, Componente3.VCC, SW1.+

custom parts:
  LCD1602-I2C: A standard character display, usually with 2x16 characters. Comes in many colors with LCM1602 IIC attached.
  KY-016 RGB Full Color LED Module: KY-016 Arduino full color 5mm RGB LED, different colors can be obtained by mixing the three primary colors.
